# Fritzing sketch 1-2-2 (saved by Fritzing 1.0.6)
breadboards: 1

parts:
  VCC1 = Battery [internal_resistance=0.1Ω]
  R1 = Resistor [tolerance=±5% power=0.25W resistance=220 package=THT]
  LED1 = LED - 5mm [color="Red (633nm)" current=0.030A package="5 mm [THT]"]

nets:
  N1: VCC1.-, LED1.cathode
  N2: VCC1.+, R1.Pin_1
  N3: R1.Pin_0, LED1.anode
