// Logisim project 1-2.circ as structural Verilog: 1 circuit, main circuit main
module main (
  input  cin,
  input  cin_2,
  input  A1,
  input  a,
  input  B1,
  input  b,
  input  A2,
  input  B2,
  input  A3,
  input  B3,
  input  A4,
  input  B4,
  output S1,
  output SUM,
  output S2,
  output Cout,
  output S3,
  output S4,
  output Cout_2
);

  wire and_1_out, and_2_out, and_3_out, and_4_out, and_5_out, and_6_out, and_7_out, and_8_out, and_9_out,
       and_10_out, or_1_out, or_2_out, or_3_out, xor_1_out, xor_2_out, xor_3_out, xor_4_out, xor_5_out,
       xor_6_out, xor_7_out, xor_8_out, xor_13_out;

  xor xor_1 (xor_1_out, cin_2, B1);
  and and_1 (and_1_out, xor_1_out, A1);
  xor xor_2 (xor_2_out, cin_2, B2);
  and and_2 (and_2_out, xor_2_out, A2);
  xor xor_3 (xor_3_out, cin_2, B3);
  and and_3 (and_3_out, xor_3_out, A3);
  xor xor_4 (xor_4_out, cin_2, B4);
  and and_4 (and_4_out, xor_4_out, A4);
  xor xor_5 (xor_5_out, A1, xor_1_out);
  or or_1 (or_1_out, and_1_out, and_5_out);
  xor xor_6 (xor_6_out, A2, xor_2_out);
  or or_2 (or_2_out, and_2_out, and_6_out);
  xor xor_7 (xor_7_out, A3, xor_3_out);
  or or_3 (or_3_out, and_3_out, and_7_out);
  xor xor_8 (xor_8_out, A4, xor_4_out);
  or or_4 (Cout_2, and_4_out, and_8_out);
  and and_5 (and_5_out, cin_2, xor_5_out);
  and and_6 (and_6_out, or_1_out, xor_6_out);
  and and_7 (and_7_out, or_2_out, xor_7_out);
  and and_8 (and_8_out, or_3_out, xor_8_out);
  xor xor_9 (S1, cin_2, xor_5_out);
  xor xor_10 (S2, or_1_out, xor_6_out);
  xor xor_11 (S3, or_2_out, xor_7_out);
  xor xor_12 (S4, or_3_out, xor_8_out);
  and and_9 (and_9_out, b, a);
  xor xor_13 (xor_13_out, a, b);
  or or_5 (Cout, and_9_out, and_10_out);
  and and_10 (and_10_out, cin, xor_13_out);
  xor xor_14 (SUM, cin, xor_13_out);
endmodule
