// Logisim project 214.circ as structural Verilog: 1 circuit, main circuit main
module main (
  input  in_1,
  input  Mode,
  input  Sin
);

  wire A_q, and_1_out, and_2_out, and_3_out, and_4_out, and_5_out, and_6_out, and_7_out, and_8_out, B_q,
       button_1_out, C_q, D_q, not_1_out, or_1_out, or_2_out, or_3_out, or_4_out;

  not not_1 (not_1_out, Mode);
  and and_1 (and_1_out, Mode, in_1);
  and and_2 (and_2_out, not_1_out, C_q);
  and and_3 (and_3_out, Mode, D_q);
  and and_4 (and_4_out, not_1_out, B_q);
  and and_5 (and_5_out, Mode, C_q);
  and and_6 (and_6_out, not_1_out, A_q);
  and and_7 (and_7_out, Mode, B_q);
  and and_8 (and_8_out, not_1_out, Sin);
  or or_1 (or_1_out, and_1_out, and_2_out);
  or or_2 (or_2_out, and_3_out, and_4_out);
  or or_3 (or_3_out, and_5_out, and_6_out);
  or or_4 (or_4_out, and_7_out, and_8_out);
  Button button_1 (.out(button_1_out));
  D_Flip_Flop D (.D(or_1_out), .clk(button_1_out), .Q(D_q));  // open: Qn, preset, reset
  D_Flip_Flop C (.D(or_2_out), .clk(button_1_out), .Q(C_q));  // open: Qn, preset, reset
  D_Flip_Flop B (.D(or_3_out), .clk(button_1_out), .Q(B_q));  // open: Qn, preset, reset
  D_Flip_Flop A (.D(or_4_out), .clk(button_1_out), .Q(A_q));  // open: Qn, preset, reset
  // Probe on D_q
  // Probe on C_q
  // Probe on B_q
  // Probe on A_q

  // Notes on the sheet:
  //   Mode: initial=0x1
  //   Sin: initial=0x1
endmodule
