// Logisim project 222.circ as structural Verilog: 1 circuit, main circuit main
module main (
  input  in_1,
  input  in_2,
  input  in_3,
  input  in_4,
  input  in_5,
  input  in_6
);

  wire A_q, and_1_out, B_q, C_q, clock_1_out, D_q, multiplexer_1_out, multiplexer_2_out, multiplexer_3_out,
       multiplexer_4_out, xnor_1_out, xor_1_out;

  Multiplexer multiplexer_1 (.in0(C_q), .in1(in_1), .out(multiplexer_1_out), .sel(in_5));
  Multiplexer multiplexer_2 (.in0(B_q), .in1(in_2), .out(multiplexer_2_out), .sel(in_5));
  Multiplexer multiplexer_3 (.in0(A_q), .in1(in_3), .out(multiplexer_3_out), .sel(in_5));
  Multiplexer multiplexer_4 (.in0(in_6), .in1(in_4), .out(multiplexer_4_out), .sel(in_5));
  Clock clock_1 (.out(clock_1_out));
  D_Flip_Flop D (.D(multiplexer_1_out), .clk(clock_1_out), .Q(D_q));  // open: Qn, preset, reset
  D_Flip_Flop C (.D(multiplexer_2_out), .clk(clock_1_out), .Q(C_q));  // open: Qn, preset, reset
  D_Flip_Flop B (.D(multiplexer_3_out), .clk(clock_1_out), .Q(B_q));  // open: Qn, preset, reset
  D_Flip_Flop A (.D(multiplexer_4_out), .clk(clock_1_out), .Q(A_q));  // open: Qn, preset, reset
  xor xor_1 (xor_1_out, D_q, C_q);
  xnor xnor_1 (xnor_1_out, B_q, A_q);
  and and_1 (and_1_out, xor_1_out, xnor_1_out);
  // Probe on and_1_out
endmodule
